// Logisim project flipflops_slides_全部电路.circ as structural Verilog: 22 circuits, main circuit s01_Gate_Delay
module s01_Gate_Delay (
  input  A,
  input  B,
  output Y
);

  and and_1 (Y, A, B);

  // Notes on the sheet:
  //   Y = A AND B (slide: Gate delay example)
endmodule

module s02_Feedback_AND (
  input  A,
  output Q
);

  and and_1 (Q, A, Q);

  // Notes on the sheet:
  //   Feedback AND: output Q fed back to input. A=0 -> Q stuck at 0
endmodule

module s02_Feedback_OR (
  input  A,
  output Q
);

  or or_1 (Q, A, Q);

  // Notes on the sheet:
  //   Feedback OR: output Q fed back to input. A=1 -> Q stuck at 1
endmodule

module s02_Feedback_NAND (
  input  A,
  output Q
);

  nand nand_1 (Q, A, Q);

  // Notes on the sheet:
  //   Feedback NAND: output Q fed back to input. A=1 -> oscillates (unsteady)
endmodule

module s02_Feedback_NOR (
  input  A,
  output Q
);

  nor nor_1 (Q, A, Q);

  // Notes on the sheet:
  //   Feedback NOR: output Q fed back to input. A=0 -> oscillates (unsteady)
endmodule

module s03_SR_Latch_NOR (
  input  R,
  input  S,
  output Q,
  output Qn
);

  nor nor_1 (Q, R, Qn);
  nor nor_2 (Qn, Q, S);

  // Notes on the sheet:
  //   NOR SR latch: R -> Q (top), S -> Qn (bottom).
  //   SR=00 hold, 01 Q=0, 10 Q=1, 11 forbidden
endmodule

module s04_SR_Latch_NAND (
  input  S_n,
  input  R_n,
  output Q,
  output Qn
);

  nand nand_1 (Q, S_n, Qn);
  nand nand_2 (Qn, Q, R_n);

  // Notes on the sheet:
  //   NAND S'R' latch (active-low): S' -> Q, R' -> Qn.
  //   S'R'=11 hold, 01 Q=1, 10 Q=0, 00 forbidden
endmodule

module Clocked_SR_Latch (
  input  S,
  input  C,
  input  R,
  output Q,
  output Qn
);

  wire nand_1_out, nand_2_out;

  nand nand_1 (nand_1_out, S, C);
  nand nand_2 (nand_2_out, C, R);
  nand nand_3 (Q, nand_1_out, Qn);
  nand nand_4 (Qn, Q, nand_2_out);

  // Notes on the sheet:
  //   Clocked (gated) SR latch: S,R only act while C=1. S=R=1 with C=1 is forbidden
endmodule

module D_Latch (
  input  D,
  input  C,
  output Q,
  output Qn
);

  wire nand_1_out, nand_2_out, not_1_out;

  not not_1 (not_1_out, D);
  nand nand_1 (nand_1_out, D, C);
  nand nand_2 (nand_2_out, C, not_1_out);
  nand nand_3 (Q, nand_1_out, Qn);
  nand nand_4 (Qn, Q, nand_2_out);

  // Notes on the sheet:
  //   Gated D latch: S=D, R=NOT D. Q follows D while C=1 (transparent), holds while C=0
endmodule

module s07_Transparency_Toggle (
  input  C,
  output Q
);

  wire d_latch_1_qn;

  D_Latch d_latch_1 (.D(d_latch_1_qn), .C(C), .Q(Q), .Qn(d_latch_1_qn));

  // Notes on the sheet:
  //   D latch with Qn fed back to D. While C=1 Q toggles endlessly (oscillation!)
endmodule

module s08_Transparency_Chain (
  input  D,
  input  C,
  output Q0,
  output Q1,
  output Q2,
  output Q3,
  output Out
);

  D_Latch d_latch_1 (.D(D), .C(C), .Q(Q0));  // open: Qn
  D_Latch d_latch_2 (.D(Q0), .C(C), .Q(Q1));  // open: Qn
  D_Latch d_latch_3 (.D(Q1), .C(C), .Q(Q2));  // open: Qn
  D_Latch d_latch_4 (.D(Q2), .C(C), .Q(Out));  // open: Qn

  assign Q3 = Out;

  // Notes on the sheet:
  //   Four D latches in series on one clock: with C=1 the input floods through all of them
endmodule

module s09_SR_MasterSlave_FF (
  input  S,
  input  C,
  input  R,
  output Q,
  output Qn
);

  wire clocked_sr_latch_1_q, clocked_sr_latch_1_qn, not_1_out;

  not not_1 (not_1_out, C);
  Clocked_SR_Latch clocked_sr_latch_1 (.S(S), .C(C), .R(R), .Q(clocked_sr_latch_1_q), .Qn(clocked_sr_latch_1_qn));
  Clocked_SR_Latch clocked_sr_latch_2 (
    .S(clocked_sr_latch_1_q), .C(not_1_out), .R(clocked_sr_latch_1_qn), .Q(Q), .Qn(Qn));

  // Notes on the sheet:
  //   SR master-slave flip-flop: master open while C=1, slave copies it when C falls (negative edge)
endmodule

module SR_MasterSlave_FF (
  input  S,
  input  C,
  input  R,
  output Q,
  output Qn
);

  wire clocked_sr_latch_1_q, clocked_sr_latch_1_qn, not_1_out;

  not not_1 (not_1_out, C);
  Clocked_SR_Latch clocked_sr_latch_1 (.S(S), .C(C), .R(R), .Q(clocked_sr_latch_1_q), .Qn(clocked_sr_latch_1_qn));
  Clocked_SR_Latch clocked_sr_latch_2 (
    .S(clocked_sr_latch_1_q), .C(not_1_out), .R(clocked_sr_latch_1_qn), .Q(Q), .Qn(Qn));

  // Notes on the sheet:
  //   SR master-slave flip-flop (negative edge) - used by the T and JK flip-flops
endmodule

module s10_D_FF_NegEdge (
  input  D,
  input  Clk,
  output Q,
  output Qn
);

  wire d_latch_1_q, d_latch_1_qn, not_1_out;

  not not_1 (not_1_out, Clk);
  D_Latch d_latch_1 (.D(D), .C(Clk), .Q(d_latch_1_q), .Qn(d_latch_1_qn));
  Clocked_SR_Latch clocked_sr_latch_1 (.S(d_latch_1_q), .C(not_1_out), .R(d_latch_1_qn), .Q(Q), .Qn(Qn));

  // Notes on the sheet:
  //   Negative-edge D flip-flop: D latch (master, C) -> SR latch (slave, NOT C). Q changes when Clk falls
endmodule

module D_FF (
  input  D,
  input  Clk,
  output Q,
  output Qn
);

  wire d_latch_1_q, d_latch_1_qn, not_1_out;

  not not_1 (not_1_out, Clk);
  D_Latch d_latch_1 (.D(D), .C(not_1_out), .Q(d_latch_1_q), .Qn(d_latch_1_qn));
  Clocked_SR_Latch clocked_sr_latch_1 (.S(d_latch_1_q), .C(Clk), .R(d_latch_1_qn), .Q(Q), .Qn(Qn));

  // Notes on the sheet:
  //   Positive-edge D flip-flop (course standard): master gets NOT Clk, slave gets Clk. Q <- D on rising edge
endmodule

module s12_T_FF (
  input  T,
  input  C,
  input  Rst,
  output Q,
  output Qn
);

  wire and_1_out, and_2_out, or_1_out;

  and and_1 (and_1_out, T, Qn);
  and and_2 (and_2_out, Q, T);
  or or_1 (or_1_out, and_2_out, Rst);
  SR_MasterSlave_FF sr_masterslave_ff_1 (.S(and_1_out), .C(C), .R(or_1_out), .Q(Q), .Qn(Qn));

  // Notes on the sheet:
  //   T flip-flop: S = T AND Qn, R = T AND Q into an SR master-slave FF.
  //   T=1: Q toggles on every falling clock edge
  //   Power-up Q is unknown (E): set Rst=1 (with T=0) and pulse C once to clear Q
endmodule

module s13_JK_FF (
  input  J,
  input  C,
  input  K,
  input  Rst,
  output Q,
  output Qn
);

  wire and_1_out, and_2_out, or_1_out;

  and and_1 (and_1_out, J, Qn);
  and and_2 (and_2_out, Q, K);
  or or_1 (or_1_out, and_2_out, Rst);
  SR_MasterSlave_FF sr_masterslave_ff_1 (.S(and_1_out), .C(C), .R(or_1_out), .Q(Q), .Qn(Qn));

  // Notes on the sheet:
  //   JK flip-flop: S = J AND Qn, R = K AND Q.
  //   JK=00 hold, 01 reset, 10 set, 11 toggle
  //   Power-up Q is unknown (E): set Rst=1 (with J=0) and pulse C once to clear Q
endmodule

module D_FF_EN (
  input  D,
  input  EN,
  input  Clk,
  output Q,
  output Qn
);

  wire multiplexer_1_out;

  Multiplexer multiplexer_1 (.in0(Q), .in1(D), .out(multiplexer_1_out), .sel(EN));
  D_FF d_ff_1 (.D(multiplexer_1_out), .Clk(Clk), .Q(Q), .Qn(Qn));

  // Notes on the sheet:
  //   D flip-flop with enable: a mux picks D when EN=1, else feeds Q back (hold)
endmodule

module s15_D_FF_SyncReset (
  input  D,
  input  Reset,
  input  Clk,
  output Q
);

  wire and_1_out, not_1_out;

  not not_1 (not_1_out, Reset);
  and and_1 (and_1_out, D, not_1_out);
  D_FF d_ff_1 (.D(and_1_out), .Clk(Clk), .Q(Q));  // open: Qn

  // Notes on the sheet:
  //   D flip-flop with synchronous reset: D_eff = D AND NOT Reset, so Q -> 0 on the next rising edge
endmodule

module s16_Shift_Register_16 (
  input  SI,
  input  Clk,
  output Q0,
  output Q1,
  output Q2,
  output Q3,
  output Q4,
  output Q5,
  output Q6,
  output Q7,
  output Q8,
  output Q9,
  output Q10,
  output Q11,
  output Q12,
  output Q13,
  output Q14,
  output Q15
);

  D_FF d_ff_1 (.D(SI), .Clk(Clk), .Q(Q0));  // open: Qn
  D_FF d_ff_2 (.D(Q0), .Clk(Clk), .Q(Q1));  // open: Qn
  D_FF d_ff_3 (.D(Q1), .Clk(Clk), .Q(Q2));  // open: Qn
  D_FF d_ff_4 (.D(Q2), .Clk(Clk), .Q(Q3));  // open: Qn
  D_FF d_ff_5 (.D(Q3), .Clk(Clk), .Q(Q4));  // open: Qn
  D_FF d_ff_6 (.D(Q4), .Clk(Clk), .Q(Q5));  // open: Qn
  D_FF d_ff_7 (.D(Q5), .Clk(Clk), .Q(Q6));  // open: Qn
  D_FF d_ff_8 (.D(Q6), .Clk(Clk), .Q(Q7));  // open: Qn
  D_FF d_ff_9 (.D(Q7), .Clk(Clk), .Q(Q8));  // open: Qn
  D_FF d_ff_10 (.D(Q8), .Clk(Clk), .Q(Q9));  // open: Qn
  D_FF d_ff_11 (.D(Q9), .Clk(Clk), .Q(Q10));  // open: Qn
  D_FF d_ff_12 (.D(Q10), .Clk(Clk), .Q(Q11));  // open: Qn
  D_FF d_ff_13 (.D(Q11), .Clk(Clk), .Q(Q12));  // open: Qn
  D_FF d_ff_14 (.D(Q12), .Clk(Clk), .Q(Q13));  // open: Qn
  D_FF d_ff_15 (.D(Q13), .Clk(Clk), .Q(Q14));  // open: Qn
  // D_FF d_ff_16: pin names not known; wires that end beside it: Q14, Clk, Q15

  // Notes on the sheet:
  //   Shift register: 16 D flip-flops in series. Each rising edge of Clk shifts SI one place right
endmodule

module s17_Load_Register_4 (
  input  D0,
  input  D1,
  input  D2,
  input  D3,
  input  Clk,
  output Q0,
  output Q1,
  output Q2,
  output Q3
);

  D_FF d_ff_1 (.D(D0), .Clk(Clk), .Q(Q0));  // open: Qn
  D_FF d_ff_2 (.D(D1), .Clk(Clk), .Q(Q1));  // open: Qn
  D_FF d_ff_3 (.D(D2), .Clk(Clk), .Q(Q2));  // open: Qn
  D_FF d_ff_4 (.D(D3), .Clk(Clk), .Q(Q3));  // open: Qn

  // Notes on the sheet:
  //   4-bit load register: every rising edge loads D0..D3 in parallel
endmodule

module s18_Load_Register_4_EN (
  input  D0,
  input  D1,
  input  D2,
  input  D3,
  input  Write,
  input  Clk,
  output Q0,
  output Q1,
  output Q2,
  output Q3
);

  D_FF_EN d_ff_en_1 (.D(D0), .EN(Write), .Clk(Clk), .Q(Q0));  // open: Qn
  D_FF_EN d_ff_en_2 (.D(D1), .EN(Write), .Clk(Clk), .Q(Q1));  // open: Qn
  D_FF_EN d_ff_en_3 (.D(D2), .EN(Write), .Clk(Clk), .Q(Q2));  // open: Qn
  D_FF_EN d_ff_en_4 (.D(D3), .EN(Write), .Clk(Clk), .Q(Q3));  // open: Qn

  // Notes on the sheet:
  //   4-bit load register with Write enable: loads only when Write=1 on a rising edge
endmodule
